# Fritzing sketch Agendamento (saved by Fritzing 0.9.3b)
circuit board: 8.46667cm x 5.64444cm
breadboards: 2

parts:
  Componente1 = Arduino Nano (Rev3.0) (ICSP)
  OMRON1 = OMRON PCB Power Relay – G5LE [part_number="G5LE-1\n" package=THT]
  OMRON2 = OMRON PCB Power Relay – G5LE [part_number="G5LE-1\n" package=THT]
  OMRON3 = OMRON PCB Power Relay – G5LE [part_number="G5LE-1\n" package=THT]
  OMRON4 = OMRON PCB Power Relay – G5LE [part_number="G5LE-1\n" package=THT]
  R1 = Resistor [tolerance=±5% resistance=10k package=THT]
  R2 = Resistor [tolerance=±5% resistance=10k package=THT]
  R3 = Resistor [tolerance=±5% resistance=10k package=THT]
  R4 = Resistor [tolerance=±5% resistance=10k package=THT]
  D1 = Diode [package=diode-1n4148]
  D2 = Diode [package=diode-1n4148]
  D3 = Diode [package=diode-1n4148]
  D4 = Diode [package=diode-1n4148]
  R5 = Resistor [tolerance=±5% resistance=100k package=THT]
  R6 = Resistor [tolerance=±5% resistance=100k package=THT]
  R7 = Resistor [tolerance=±5% resistance=100k package=THT]
  R8 = Resistor [tolerance=±5% resistance=100k package=THT]
  C1 = Electrolytic Capacitor [capacitance=1µF package="100 mil [THT, electrolytic]"]
  J1 = Power Jack [package=power_jack_slot]
  J2 = female pin header, 3 pins [form="♀ (female)"]
  LCD1 = LCD screen
  R11 = TRIMPOT [package=3386u]
  btnMode = Momentary Switch [package=tactile-pth]
  btnUp = Momentary Switch [package=tactile-pth]
  btnDown = Momentary Switch [package=tactile-pth]
  btnSet = Momentary Switch [package=tactile-pth]
  C2 = Capacitor [package=cap-pth-small2]
  C3 = Capacitor [package=cap-pth-small2]
  Q1 = NPN-Transistor [package="TO92 [THT]"]
  Q2 = NPN-Transistor [package="TO92 [THT]"]
  Q3 = NPN-Transistor [package="TO92 [THT]"]
  Q4 = NPN-Transistor [package="TO92 [THT]"]
  C4 = Capacitor [package=cap-pth-small2]
  C5 = Capacitor [package=cap-pth-small2]
  R9 = Resistor [tolerance=±5% resistance=10k package=THT]
  R10 = Resistor [tolerance=±5% resistance=10k package=THT]
  R11_2 = Resistor [tolerance=±5% resistance=10k package=THT]
  R12 = Resistor [tolerance=±5% resistance=10k package=THT]
  J3 = male pin header, 9 pins [form="♂ (male)"]
  MH-Real-Time_Clock_Module_3 = RTC_DS1302_module
  R13 = Resistor [tolerance=±5% resistance=220 package=THT]
  LED1 = LED - 3mm [color="Red (633nm)" package="3 mm [THT]"]

nets:
  GND: Componente1.GND, R5.Pin_1, R6.Pin_1, R7.Pin_1, R8.Pin_1, C1.-, J1.GNDBREAK, J2.pin3, LCD1.VSS, LCD1.R/W, LCD1.LED-, R11.CCW, btnMode.1, btnMode.2, btnUp.1, btnUp.2, btnDown.1, btnDown.2, btnSet.1, btnSet.2, C2.1, C3.1, Q1.E, Q2.E, Q3.E, Q4.E, C4.1, C5.1, J3.pin1, MH-Real-Time_Clock_Module_3.GND, LED1.cathode
  N1: Componente1.D2, MH-Real-Time_Clock_Module_3.RST
  N2: Componente1.D3, MH-Real-Time_Clock_Module_3.DAT
  DB4: Componente1.D4, LCD1.DB4
  DB5: Componente1.D5, LCD1.DB5
  DB6: Componente1.D6, LCD1.DB6
  DB7: Componente1.D7, LCD1.DB7
  RS: Componente1.D8, LCD1.RS
  E: Componente1.D9, LCD1.E
  N3: Componente1.D10, MH-Real-Time_Clock_Module_3.CLK
  5V: Componente1.5V, OMRON1.COIL2, OMRON2.COIL2, OMRON3.COIL2, OMRON4.COIL2, D1.C, D2.C, D3.C, D4.C, C1.+, J1.PWR, LCD1.VDD, LCD1.LED+, R11.CW, R9.Pin_1, R10.Pin_1, R11_2.Pin_1, R12.Pin_1, MH-Real-Time_Clock_Module_3.VCC, R13.Pin_1
  btn4: Componente1.A7, btnSet.3, btnSet.4, C5.2, R12.Pin_0
  btn3: Componente1.A6, btnDown.3, btnDown.4, C4.2, R11_2.Pin_0
  btn2: Componente1.A5, btnUp.3, btnUp.4, C3.2, R10.Pin_0
  btn1: Componente1.A4, btnMode.3, btnMode.4, C2.2, R9.Pin_0
  DO4: Componente1.A3, R4.Pin_1
  DO3: Componente1.A2, R3.Pin_1
  DO2: Componente1.A1, R2.Pin_1
  DO1: Componente1.A0, R1.Pin_1
  3.3V: Componente1.3V3, J2.pin1
  N4: OMRON1.A, J3.pin8
  N5: OMRON1.COIL1, D1.A, Q1.C
  N6: OMRON1.C, OMRON2.C, OMRON3.C, OMRON4.C, J2.pin2
  N7: OMRON1.B, J3.pin9
  N8: OMRON2.A, J3.pin6
  N9: OMRON2.COIL1, D2.A, Q2.C
  N10: OMRON2.B, J3.pin7
  N11: OMRON3.A, J3.pin4
  N12: OMRON3.COIL1, D3.A, Q3.C
  N13: OMRON3.B, J3.pin5
  N14: OMRON4.A, J3.pin2
  N15: OMRON4.COIL1, D4.A, Q4.C
  N16: OMRON4.B, J3.pin3
  N17: R1.Pin_0, R5.Pin_0, Q1.B
  N18: R2.Pin_0, R6.Pin_0, Q2.B
  N19: R3.Pin_0, R7.Pin_0, Q3.B
  N20: R4.Pin_0, R8.Pin_0, Q4.B
  N21: LCD1.V0, R11.WIPER
  N22: R13.Pin_0, LED1.anode

notes:
  Saídas
  Interface Homem-Máquina
  CPU
  Alimentação

custom parts:
  RTC_DS1302_module: Arduino module DS1302 SPI Real Time Clock
