# Fritzing sketch Datalogger uBox (saved by Fritzing 0.9.3b)
circuit board: 8.46667cm x 5.64444cm
breadboards: 1

parts:
  U1 = RJ45 Jack [package=rj45-8]
  U2 = 74HC595 SMD [package="SO16 [SMD]"]
  C1 = Ceramic Capacitor [capacitance=100nF package="100 mil [THT, multilayer]"]

nets:
  N1: U1.1, U2.DS
  N2: U1.8, C1.1
  N3: U2.Q0, U2.VCC
